// Logisim project CPU.circ as structural Verilog: 1 circuit, main circuit main
module main (
  input  [1:0] in_1,
  input  [1:0] in_2,
  output [7:0] out_3,
  output [7:0] out_4,
  output out_5,
  output out_6,
  output out_7,
  output out_8,
  output out_9,
  output [7:0] out_10,
  output [7:0] out_11
);

  wire and_1_out, and_2_out, and_3_out, and_4_out, clock_1_out, clock_2_out, decoder_1_out0, decoder_1_out1,
       decoder_1_out2, decoder_1_out3;
  wire [1:0] Storage_Ram_dout_3;
  wire [3:0] Storage_Ram_dout_2;
  wire [7:0] adder_1_out, adder_2_out, PC_q, ram_1_dout, subtractor_1_out, X0_q, X1_q, X2_q, X3_q;
  wire [10:0] Storage_Ram_dout;

  Adder adder_1 (.a(PC_q), .b(8'h1), .out(adder_1_out));  // open: cin, cout
  Clock #(.highDuration(4), .lowDuration(4)) clock_1 (.out(clock_1_out));
  Register PC (.D(adder_1_out), .en(1'b1), .clk(clock_1_out), .Q(PC_q));  // open: clr
  RAM #(.dataWidth(16)) Storage_Ram (
    .addr(PC_q), .we(1'b0), .oe(1'b1), .clk(clock_1_out),
    .dout({out_9, out_8, out_7, out_6, out_5, Storage_Ram_dout[10], Storage_Ram_dout_3[1], Storage_Ram_dout[8], Storage_Ram_dout_3[0], Storage_Ram_dout[6], Storage_Ram_dout_2, Storage_Ram_dout[1:0]}));  // open: din
  Decoder #(.select(2)) decoder_1 (
    .out0(decoder_1_out0), .out1(decoder_1_out1), .out2(decoder_1_out2), .out3(decoder_1_out3),
    .sel(Storage_Ram_dout[1:0]));  // open: en
  and and_1 (and_1_out, decoder_1_out0, Storage_Ram_dout[8]);
  and and_2 (and_2_out, decoder_1_out1, Storage_Ram_dout[8]);
  and and_3 (and_3_out, decoder_1_out2, Storage_Ram_dout[8]);
  and and_4 (and_4_out, decoder_1_out3, Storage_Ram_dout[8]);
  Register X0 (.D(out_11), .en(and_1_out), .clk(clock_1_out), .Q(X0_q));  // open: clr
  Register X1 (.D(out_11), .en(and_2_out), .clk(clock_1_out), .Q(X1_q));  // open: clr
  Register X2 (.D(out_11), .en(and_3_out), .clk(clock_1_out), .Q(X2_q));  // open: clr
  Register X3 (.D(out_11), .en(and_4_out), .clk(clock_1_out), .Q(X3_q));  // open: clr
  Hex_Digit_Display #(.decimalPoint("false")) R0 (.value(X0_q[7:4]));
  Hex_Digit_Display #(.decimalPoint("false")) hex_digit_display_1 (.value(X0_q[3:0]));
  Hex_Digit_Display #(.decimalPoint("false")) R1 (.value(X1_q[7:4]));
  Hex_Digit_Display #(.decimalPoint("false")) hex_digit_display_2 (.value(X1_q[3:0]));
  Hex_Digit_Display #(.decimalPoint("false")) R2 (.value(X2_q[7:4]));
  Multiplexer #(.select(2), .width(8)) multiplexer_1 (
    .in0(X0_q), .in1(X1_q), .in2(X2_q), .in3(X3_q), .out(out_3), .sel(Storage_Ram_dout_2[1:0]));
  Multiplexer #(.select(2), .width(8)) multiplexer_2 (
    .in0(X0_q), .in1(X1_q), .in2(X2_q), .in3(X3_q), .out(out_10), .sel(Storage_Ram_dout_2[3:2]));
  Hex_Digit_Display #(.decimalPoint("false")) hex_digit_display_3 (.value(X2_q[3:0]));
  Hex_Digit_Display #(.decimalPoint("false")) R3 (.value(X3_q[7:4]));
  Hex_Digit_Display #(.decimalPoint("false")) hex_digit_display_4 (.value(X3_q[3:0]));
  Hex_Digit_Display #(.decimalPoint("false")) ALUOUT (.value(out_11[7:4]));
  Hex_Digit_Display #(.decimalPoint("false")) hex_digit_display_5 (.value(out_11[3:0]));
  Adder adder_2 (.a(out_3), .b(out_10), .out(adder_2_out));  // open: cin, cout
  Subtractor subtractor_1 (.a(out_10), .b(out_3), .out(subtractor_1_out));  // open: bin, bout
  Multiplexer #(.width(8)) multiplexer_3 (
    .in0(adder_2_out), .in1(subtractor_1_out), .out(out_4), .sel(Storage_Ram_dout[6]));
  Clock clock_2 (.out(clock_2_out));
  RAM ram_1 (.addr(out_4), .oe(Storage_Ram_dout[10]), .clk(clock_2_out), .dout(ram_1_dout));  // open: we, din
  Multiplexer #(.select(2), .width(8)) multiplexer_4 (
    .in0(out_4), .in1(ram_1_dout), .in2({in_2, in_1, Storage_Ram_dout_2}), .out(out_11),
    .sel(Storage_Ram_dout_3));  // open: in3

  // Notes on the sheet:
  //   Constant
  //   Write_Enable_Pin
  //   Mem_Write_Enable
  //   Mem_Output_Enable
  //   Adder
  //   Clock
  //   Yousaf Rajput
  //   I pledge my Honor that i have abided by the Stevens Honor System
  //   CPU: Jet Z16
  //   Instruction Mem
  //   RegDataW
  //   WriteReg
  //   ReadReg1
  //   ReadReg2
  //   Add/Sub
  //   MemToReg
  //   RegWrite
  //   ImmToReg
  //   MemRead
  //   4 to 8 bit immediate from bits 2-5
  //   RegData1
  //   RegData2
  //   ALUout
  //   Ram Clock
  //   Data Memory
endmodule
